# Fritzing sketch Torch (saved by Fritzing 0.9.3b)

parts:
  Arduino1 = Arduino Nano (Rev3.0)
  S1 = Pushbutton [package="[THT]"]
  S2 = Pushbutton [package="[THT]"]
  S3 = Pushbutton [package="[THT]"]
  R1 = Resistor [tolerance=±5% resistance=220 package=THT]
  D1 = Rectifier Diode [part_number=1N4001 package="300 mil [THT]"]
  D2 = Rectifier Diode [part_number=1N4001 package="300 mil [THT]"]
  D3 = Rectifier Diode [part_number=1N4001 package="300 mil [THT]"]
  RGB_SMD_LED1 = SMD RGB LED (WS2812) [package=5050]
  J1 = Power Jack [package=power_jack_slot]

nets:
  N1: Arduino1.D2, D1.anode
  N2: Arduino1.D4, S3.Pin_3, S3.Pin_4, D3.cathode
  N3: Arduino1.D5, D2.cathode
  N4: Arduino1.D6, S1.Pin_1, S1.Pin_2, D1.cathode
  N5: Arduino1.5V, J1.PWR
  N6: Arduino1.D13/SCK, R1.Pin_0
  N7: S2.Pin_1, S2.Pin_2
  N8: R1.Pin_1, RGB_SMD_LED1.DIn

notes:
  BLINK

// code stored in the sketch: Blink.ino
/*
  Blink
  
  Switching a LED on and off
  
  This example is part of the Fritzing Creator Kit: www.fritzing.org/creator-kit.
*/

int led = 13;                   // integer variable led is declared

void setup() {                  // the setup() method is executed only once
  pinMode(led, OUTPUT);         // the led PIN is declared as digital output
}

void loop() {                   // the loop() method is repeated
  digitalWrite(led, HIGH);      // switching on the led 
  delay(1000);                  // stopping the program for 1000 milliseconds
  digitalWrite(led, LOW);       // switching off the led 
  delay(1000);                  // stopping the program for 1000 milliseconds
}
